# Fritzing sketch triple-led (saved by Fritzing 0.8.5b)
breadboards: 1

parts:
  R1 = Resistor [tolerance=±5% resistance=220 package=THT]
  R2 = Resistor [tolerance=±5% resistance=220 package=THT]
  R3 = Resistor [tolerance=±5% resistance=220 package=THT]
  LED1 = LED - 5mm [color="Red (633nm)" package="5 mm [THT]"]
  LED2 = LED - 5mm [color="Red (633nm)" package="5 mm [THT]"]
  LED3 = LED - 5mm [color="Red (633nm)" package="5 mm [THT]"]

nets:
  N1: R1.Pin_0, LED1.cathode
  N2: R1.Pin_1, R2.Pin_1, R3.Pin_1
  N3: R2.Pin_0, LED2.cathode
  N4: R3.Pin_0, LED3.cathode

notes:
  GP0
  GP1
  GP2
  GND
